// Logisim project crc.circ as structural Verilog: 2 circuits, main circuit CRC
module _4bit_divisor (
  input  A3,
  input  A2,
  input  A1,
  input  A0,
  input  [3:0] B,
  output B3,
  output B2,
  output B1,
  output B0
);

  wire [3:0] xor_1_out;

  assign xor_1_out = {A3, A2, A1, A0} ^ B;  // XOR_Gate xor_1, 4 bits wide
  Multiplexer #(.width(4), .enable("false")) multiplexer_1 (
    .in0({A3, A2, A1, A0}), .in1(xor_1_out), .out({B3, B2, B1, B0}), .sel(A3));
endmodule

module CRC (
  input  [7:0] A,
  input  [3:0] B,
  output [10:0] out_3
);

  wire n4bit_divisor_1_b0, n4bit_divisor_1_b1, n4bit_divisor_1_b2, n4bit_divisor_2_b0, n4bit_divisor_2_b1,
       n4bit_divisor_2_b2, n4bit_divisor_3_b0, n4bit_divisor_3_b1, n4bit_divisor_3_b2, n4bit_divisor_4_b0,
       n4bit_divisor_4_b1, n4bit_divisor_4_b2, n4bit_divisor_5_b0, n4bit_divisor_5_b1, n4bit_divisor_5_b2,
       n4bit_divisor_6_b0, n4bit_divisor_6_b1, n4bit_divisor_6_b2, n4bit_divisor_7_b0, n4bit_divisor_7_b1,
       n4bit_divisor_7_b2;

  _4bit_divisor u_4bit_divisor_1 (
    .A3(A[7]), .A2(A[6]), .A1(A[5]), .A0(A[4]), .B(B), .B2(n4bit_divisor_1_b2), .B1(n4bit_divisor_1_b1),
    .B0(n4bit_divisor_1_b0));  // open: B3
  _4bit_divisor u_4bit_divisor_2 (
    .A3(n4bit_divisor_1_b2), .A2(n4bit_divisor_1_b1), .A1(n4bit_divisor_1_b0), .A0(A[3]), .B(B),
    .B2(n4bit_divisor_2_b2), .B1(n4bit_divisor_2_b1), .B0(n4bit_divisor_2_b0));  // open: B3
  _4bit_divisor u_4bit_divisor_3 (
    .A3(n4bit_divisor_2_b2), .A2(n4bit_divisor_2_b1), .A1(n4bit_divisor_2_b0), .A0(A[2]), .B(B),
    .B2(n4bit_divisor_3_b2), .B1(n4bit_divisor_3_b1), .B0(n4bit_divisor_3_b0));  // open: B3
  _4bit_divisor u_4bit_divisor_4 (
    .A3(n4bit_divisor_3_b2), .A2(n4bit_divisor_3_b1), .A1(n4bit_divisor_3_b0), .A0(A[1]), .B(B),
    .B2(n4bit_divisor_4_b2), .B1(n4bit_divisor_4_b1), .B0(n4bit_divisor_4_b0));  // open: B3
  _4bit_divisor u_4bit_divisor_5 (
    .A3(n4bit_divisor_4_b2), .A2(n4bit_divisor_4_b1), .A1(n4bit_divisor_4_b0), .A0(A[0]), .B(B),
    .B2(n4bit_divisor_5_b2), .B1(n4bit_divisor_5_b1), .B0(n4bit_divisor_5_b0));  // open: B3
  _4bit_divisor u_4bit_divisor_6 (
    .A3(n4bit_divisor_5_b2), .A2(n4bit_divisor_5_b1), .A1(n4bit_divisor_5_b0), .A0(1'b0), .B(B),
    .B2(n4bit_divisor_6_b2), .B1(n4bit_divisor_6_b1), .B0(n4bit_divisor_6_b0));  // open: B3
  _4bit_divisor u_4bit_divisor_7 (
    .A3(n4bit_divisor_6_b2), .A2(n4bit_divisor_6_b1), .A1(n4bit_divisor_6_b0), .A0(1'b0), .B(B),
    .B2(n4bit_divisor_7_b2), .B1(n4bit_divisor_7_b1), .B0(n4bit_divisor_7_b0));  // open: B3
  _4bit_divisor u_4bit_divisor_8 (
    .A3(n4bit_divisor_7_b2), .A2(n4bit_divisor_7_b1), .A1(n4bit_divisor_7_b0), .A0(1'b0), .B(B),
    .B2(out_3[2]), .B1(out_3[1]), .B0(out_3[0]));  // open: B3

  assign out_3[10:3] = A;
endmodule
