// Logisim project grf.circ as structural Verilog
module grf (
  input  clk,
  input  rst,
  input  WE,
  input  [4:0] A1,
  input  [4:0] A2,
  input  [4:0] A3,
  input  [31:0] WD,
  output [31:0] RD1,
  output [31:0] RD2
);

  wire we_0, we_1, we_2, we_3, we_4, we_5, we_6, we_7, we_8, we_9, we_10, we_11, we_12, we_13, we_14, we_15,
       we_16, we_17, we_18, we_19, we_20, we_21, we_22, we_23, we_24, we_25, we_26, we_27, we_28, we_29,
       we_30, we_31;
  wire [31:0] rd_1, rd_2, rd_3, rd_4, rd_5, rd_6, rd_7, rd_8, rd_9, rd_10, rd_11, rd_12, rd_13, rd_14, rd_15,
       rd_16, rd_17, rd_18, rd_19, rd_20, rd_21, rd_22, rd_23, rd_24, rd_25, rd_26, rd_27, rd_28, rd_29,
       rd_30, rd_31;

  Register #(.width(32)) register_1 (.D(WD), .en(we_1), .Q(rd_1), .clk(clk), .clr(rst));
  Register #(.width(32)) register_2 (.D(WD), .en(we_2), .Q(rd_2), .clk(clk), .clr(rst));
  Register #(.width(32)) register_3 (.D(WD), .en(we_3), .Q(rd_3), .clk(clk), .clr(rst));
  Register #(.width(32)) register_4 (.D(WD), .en(we_4), .Q(rd_4), .clk(clk), .clr(rst));
  Register #(.width(32)) register_5 (.D(WD), .en(we_5), .Q(rd_5), .clk(clk), .clr(rst));
  Register #(.width(32)) register_6 (.D(WD), .en(we_6), .Q(rd_6), .clk(clk), .clr(rst));
  Register #(.width(32)) register_7 (.D(WD), .en(we_7), .Q(rd_7), .clk(clk), .clr(rst));
  Demultiplexer #(.select(5), .enable("false")) demultiplexer_1 (
    .out0(we_0), .out1(we_1), .out2(we_2), .out3(we_3), .out4(we_4), .out5(we_5), .out6(we_6), .out7(we_7),
    .out8(we_8), .out9(we_9), .out10(we_10), .out11(we_11), .out12(we_12), .out13(we_13), .out14(we_14),
    .out15(we_15), .out16(we_16), .out17(we_17), .out18(we_18), .out19(we_19), .out20(we_20), .out21(we_21),
    .out22(we_22), .out23(we_23), .out24(we_24), .out25(we_25), .out26(we_26), .out27(we_27), .out28(we_28),
    .out29(we_29), .out30(we_30), .out31(we_31), .in(WE), .sel(A3));
  Register #(.width(32)) register_8 (.D(WD), .en(we_8), .Q(rd_8), .clk(clk), .clr(rst));
  Register #(.width(32)) register_9 (.D(WD), .en(we_9), .Q(rd_9), .clk(clk), .clr(rst));
  Register #(.width(32)) register_10 (.D(WD), .en(we_10), .Q(rd_10), .clk(clk), .clr(rst));
  Register #(.width(32)) register_11 (.D(WD), .en(we_11), .Q(rd_11), .clk(clk), .clr(rst));
  Register #(.width(32)) register_12 (.D(WD), .en(we_12), .Q(rd_12), .clk(clk), .clr(rst));
  Register #(.width(32)) register_13 (.D(WD), .en(we_13), .Q(rd_13), .clk(clk), .clr(rst));
  Register #(.width(32)) register_14 (.D(WD), .en(we_14), .Q(rd_14), .clk(clk), .clr(rst));
  Register #(.width(32)) register_15 (.D(WD), .en(we_15), .Q(rd_15), .clk(clk), .clr(rst));
  Register #(.width(32)) register_16 (.D(WD), .en(we_16), .Q(rd_16), .clk(clk), .clr(rst));
  Register #(.width(32)) register_17 (.D(WD), .en(we_17), .Q(rd_17), .clk(clk), .clr(rst));
  Register #(.width(32)) register_18 (.D(WD), .en(we_18), .Q(rd_18), .clk(clk), .clr(rst));
  Register #(.width(32)) register_19 (.D(WD), .en(we_19), .Q(rd_19), .clk(clk), .clr(rst));
  Register #(.width(32)) register_20 (.D(WD), .en(we_20), .Q(rd_20), .clk(clk), .clr(rst));
  Register #(.width(32)) register_21 (.D(WD), .en(we_21), .Q(rd_21), .clk(clk), .clr(rst));
  Register #(.width(32)) register_22 (.D(WD), .en(we_22), .Q(rd_22), .clk(clk), .clr(rst));
  Register #(.width(32)) register_23 (.D(WD), .en(we_23), .Q(rd_23), .clk(clk), .clr(rst));
  Register #(.width(32)) register_24 (.D(WD), .en(we_24), .Q(rd_24), .clk(clk), .clr(rst));
  Register #(.width(32)) register_25 (.D(WD), .en(we_25), .Q(rd_25), .clk(clk), .clr(rst));
  Register #(.width(32)) register_26 (.D(WD), .en(we_26), .Q(rd_26), .clk(clk), .clr(rst));
  Register #(.width(32)) register_27 (.D(WD), .en(we_27), .Q(rd_27), .clk(clk), .clr(rst));
  Register #(.width(32)) register_28 (.D(WD), .en(we_28), .Q(rd_28), .clk(clk), .clr(rst));
  Register #(.width(32)) register_29 (.D(WD), .en(we_29), .Q(rd_29), .clk(clk), .clr(rst));
  Register #(.width(32)) register_30 (.D(WD), .en(we_30), .Q(rd_30), .clk(clk), .clr(rst));
  Register #(.width(32)) register_31 (.D(WD), .en(we_31), .Q(rd_31), .clk(clk), .clr(rst));
  Multiplexer #(.select(5), .width(32), .enable("false")) multiplexer_1 (
    .in0({32{1'b0}}), .in1(rd_1), .in2(rd_2), .in3(rd_3), .in4(rd_4), .in5(rd_5), .in6(rd_6), .in7(rd_7),
    .in8(rd_8), .in9(rd_9), .in10(rd_10), .in11(rd_11), .in12(rd_12), .in13(rd_13), .in14(rd_14),
    .in15(rd_15), .in16(rd_16), .in17(rd_17), .in18(rd_18), .in19(rd_19), .in20(rd_20), .in21(rd_21),
    .in22(rd_22), .in23(rd_23), .in24(rd_24), .in25(rd_25), .in26(rd_26), .in27(rd_27), .in28(rd_28),
    .in29(rd_29), .in30(rd_30), .in31(rd_31), .out(RD1), .sel(A1));
  Multiplexer #(.select(5), .width(32), .enable("false")) multiplexer_2 (
    .in0({32{1'b0}}), .in1(rd_1), .in2(rd_2), .in3(rd_3), .in4(rd_4), .in5(rd_5), .in6(rd_6), .in7(rd_7),
    .in8(rd_8), .in9(rd_9), .in10(rd_10), .in11(rd_11), .in12(rd_12), .in13(rd_13), .in14(rd_14),
    .in15(rd_15), .in16(rd_16), .in17(rd_17), .in18(rd_18), .in19(rd_19), .in20(rd_20), .in21(rd_21),
    .in22(rd_22), .in23(rd_23), .in24(rd_24), .in25(rd_25), .in26(rd_26), .in27(rd_27), .in28(rd_28),
    .in29(rd_29), .in30(rd_30), .in31(rd_31), .out(RD2), .sel(A2));
endmodule
