// Logisim project string-detect.circ as structural Verilog: 3 circuits, main circuit fsm
module fsm (
  input  CLR,
  input  [1:0] In,
  output Z
);

  wire clock_1_out;
  wire [1:0] multiplexer_1_out, register_1_q, state_trans_1_s0_;

  Clock clock_1 (.out(clock_1_out));
  state_trans state_trans_1 (
    .S1(register_1_q[0]), .S0(register_1_q[1]), .I1(In[1]), .I0(In[0]), .S1_(state_trans_1_s0_[1]),
    .S0_(state_trans_1_s0_[0]));
  Multiplexer #(.width(2), .enable("false")) multiplexer_1 (
    .in0(state_trans_1_s0_), .in1(2'b00), .out(multiplexer_1_out), .sel(CLR));
  Register #(.width(2)) register_1 (.D(multiplexer_1_out), .Q(register_1_q), .clk(clock_1_out));  // open: en, clr
  \output  output_1 (.S1(register_1_q[1]), .S0(register_1_q[0]), .I1(In[1]), .I0(In[0]), .O(Z));
endmodule

module state_trans (
  input  S1,
  input  S0,
  input  I1,
  input  I0,
  output S1_,
  output S0_
);

  wire and_1_out, and_2_out, and_3_out, and_4_out, and_5_out, and_6_out, and_7_out, and_8_out, not_1_out,
       not_2_out, not_3_out, not_4_out, not_5_out, not_6_out, not_7_out, not_8_out, not_9_out, not_10_out,
       not_11_out, not_12_out, not_13_out, not_14_out, not_15_out, not_16_out;

  not not_1 (not_1_out, S1);
  and and_1 (and_1_out, not_1_out, S0, not_2_out);
  not not_2 (not_2_out, I1);
  not not_3 (not_3_out, S1);
  and and_2 (and_2_out, not_3_out, S0, not_4_out);
  not not_4 (not_4_out, I0);
  and and_3 (and_3_out, S1, not_5_out, not_6_out);
  not not_5 (not_5_out, S0);
  not not_6 (not_6_out, I1);
  not not_7 (not_7_out, S0);
  and and_4 (and_4_out, S1, not_7_out, not_8_out);
  not not_8 (not_8_out, I0);
  not not_9 (not_9_out, I1);
  and and_5 (and_5_out, S1, not_9_out, I0);
  not not_10 (not_10_out, S1);
  not not_11 (not_11_out, S0);
  not not_12 (not_12_out, I1);
  not not_13 (not_13_out, S1);
  not not_14 (not_14_out, I0);
  not not_15 (not_15_out, S0);
  not not_16 (not_16_out, I0);
  or or_1 (S1_, and_1_out, and_2_out, and_3_out, and_4_out, and_5_out);
  and and_6 (and_6_out, not_10_out, not_11_out, not_12_out, I0);
  or or_2 (S0_, and_6_out, and_7_out, and_8_out);
  and and_7 (and_7_out, not_13_out, S0, not_14_out);
  and and_8 (and_8_out, S1, not_15_out, not_16_out);
endmodule

module \output  (
  input  S1,
  input  S0,
  input  I1,
  input  I0,
  output O
);

  wire not_1_out;

  and and_1 (O, S1, S0, not_1_out);
  not not_1 (not_1_out, I0);
endmodule
