// Logisim project 4bit_sort.circ as structural Verilog: 3 circuits, main circuit 1bit_swap
module _1bit_swap (
  input  I1,
  input  I2,
  input  S,
  output O1,
  output O2
);

  wire and_1_out, and_2_out, and_3_out, and_4_out, not_1_out;

  not not_1 (not_1_out, S);
  and and_1 (and_1_out, I1, not_1_out);
  and and_2 (and_2_out, I2, S);
  and and_3 (and_3_out, I2, not_1_out);
  and and_4 (and_4_out, I1, S);
  or or_1 (O1, and_1_out, and_2_out);
  or or_2 (O2, and_3_out, and_4_out);
endmodule

module _4bit_swap (
  input  [3:0] in_1,
  input  [3:0] in_2,
  input  in_3,
  output [3:0] out_4,
  output [3:0] out_5
);

  _1bit_swap u_1bit_swap_1 (.I1(in_1[0]), .I2(in_2[0]), .S(in_3), .O1(out_4[0]), .O2(out_5[0]));
  _1bit_swap u_1bit_swap_2 (.I1(in_1[1]), .I2(in_2[1]), .S(in_3), .O1(out_4[1]), .O2(out_5[1]));
  _1bit_swap u_1bit_swap_3 (.I1(in_1[2]), .I2(in_2[2]), .S(in_3), .O1(out_4[2]), .O2(out_5[2]));
  _1bit_swap u_1bit_swap_4 (.I1(in_1[3]), .I2(in_2[3]), .S(in_3), .O1(out_4[3]), .O2(out_5[3]));
endmodule

module _4bit_sort (
  input  [3:0] A,
  input  [3:0] B,
  input  [3:0] C,
  input  [3:0] D,
  output [3:0] _1,
  output [3:0] _2,
  output [3:0] _3,
  output [3:0] _4
);

  wire comparator_1_gt, comparator_2_gt, comparator_3_gt, comparator_4_gt, comparator_5_gt, comparator_6_gt;
  wire [3:0] n4bit_swap_1_out_4, n4bit_swap_1_out_5, n4bit_swap_2_out_4, n4bit_swap_2_out_5,
       n4bit_swap_3_out_4, n4bit_swap_3_out_5, n4bit_swap_4_out_5, n4bit_swap_5_out_5;

  _4bit_swap u_4bit_swap_1 (
    .in_1(C), .in_2(D), .in_3(comparator_1_gt), .out_4(n4bit_swap_1_out_4), .out_5(n4bit_swap_1_out_5));
  Comparator #(.width(4), .mode("unsigned")) comparator_1 (.a(C), .b(D), .gt(comparator_1_gt));  // open: eq, lt
  _4bit_swap u_4bit_swap_2 (
    .in_1(B), .in_2(n4bit_swap_1_out_4), .in_3(comparator_2_gt), .out_4(n4bit_swap_2_out_4),
    .out_5(n4bit_swap_2_out_5));
  Comparator #(.width(4), .mode("unsigned")) comparator_2 (
    .a(B), .b(n4bit_swap_1_out_4), .gt(comparator_2_gt));  // open: eq, lt
  _4bit_swap u_4bit_swap_3 (
    .in_1(n4bit_swap_2_out_5), .in_2(n4bit_swap_1_out_5), .in_3(comparator_3_gt), .out_4(n4bit_swap_3_out_4),
    .out_5(n4bit_swap_3_out_5));
  Comparator #(.width(4), .mode("unsigned")) comparator_3 (
    .a(n4bit_swap_2_out_5), .b(n4bit_swap_1_out_5), .gt(comparator_3_gt));  // open: eq, lt
  Comparator #(.width(4), .mode("unsigned")) comparator_4 (
    .a(A), .b(n4bit_swap_2_out_4), .gt(comparator_4_gt));  // open: eq, lt
  _4bit_swap u_4bit_swap_4 (
    .in_1(A), .in_2(n4bit_swap_2_out_4), .in_3(comparator_4_gt), .out_4(_1), .out_5(n4bit_swap_4_out_5));
  _4bit_swap u_4bit_swap_5 (
    .in_1(n4bit_swap_4_out_5), .in_2(n4bit_swap_3_out_4), .in_3(comparator_5_gt), .out_4(_2),
    .out_5(n4bit_swap_5_out_5));
  Comparator #(.width(4), .mode("unsigned")) comparator_5 (
    .a(n4bit_swap_4_out_5), .b(n4bit_swap_3_out_4), .gt(comparator_5_gt));  // open: eq, lt
  Comparator #(.width(4), .mode("unsigned")) comparator_6 (
    .a(n4bit_swap_5_out_5), .b(n4bit_swap_3_out_5), .gt(comparator_6_gt));  // open: eq, lt
  _4bit_swap u_4bit_swap_6 (
    .in_1(n4bit_swap_5_out_5), .in_2(n4bit_swap_3_out_5), .in_3(comparator_6_gt), .out_4(_3), .out_5(_4));
endmodule
