// Logisim project fib.circ as structural Verilog: 1 circuit, main circuit main
module main (
  input  [2:0] N,
  output [3:0] Nth
);

  wire clk, comparator_1_eq, comparator_1_gt, first_posedge, not_1_out, or_1_out;
  wire [31:0] adder_1_out, bit_extender_1_out, counter_1_q, multiplexer_1_out, multiplexer_2_out,
       register_1_q, register_2_q;

  Counter #(.width(32), .max('hffffffff)) counter_1 (.Q(counter_1_q), .clk(clk));  // open: load, D, count, carry, clr
  assign bit_extender_1_out = {{29{1'b0}}, N};  // Bit_Extender bit_extender_1
  Comparator #(.width(32), .mode("unsigned")) comparator_1 (
    .a(counter_1_q), .b(bit_extender_1_out), .gt(comparator_1_gt), .eq(comparator_1_eq));  // open: lt
  not not_1 (not_1_out, or_1_out);
  Clock clock_1 (.out(clk));
  Register #(.width(1)) first_posedge_done (.D(1'b1), .Q(first_posedge), .clk(clk));  // open: en, clr
  or or_1 (or_1_out, comparator_1_gt, comparator_1_eq);
  Multiplexer #(.width(32), .disabled(0), .enable("false")) multiplexer_1 (
    .in0(32'h1), .in1(adder_1_out), .out(multiplexer_1_out), .sel(first_posedge));
  Register #(.width(32)) register_1 (.D(multiplexer_1_out), .en(not_1_out), .Q(register_1_q), .clk(clk));  // open: clr
  Multiplexer #(.width(32), .disabled(0), .enable("false")) multiplexer_2 (
    .in0(32'h1), .in1(register_1_q), .out(multiplexer_2_out), .sel(first_posedge));
  Register #(.width(32)) register_2 (.D(multiplexer_2_out), .en(not_1_out), .Q(register_2_q), .clk(clk));  // open: clr
  BitSelector #(.width(32), .group(4)) bitselector_1 (.in(register_2_q), .out(Nth), .sel(3'b000));
  Adder #(.width(32)) adder_1 (.a(register_1_q), .b(register_2_q), .out(adder_1_out));  // open: cin, cout
endmodule
