// Logisim project fib2.circ as structural Verilog: 8 circuits, main circuit main
module main (
  input  [31:0] N,
  output [31:0] Nth
);

  wire buf_q, clk, counter_1_carry, not_1_out, not_2_out, not_3_out, one, or_1_out, register_1_q,
       shift_register_1_out, zero;
  wire [1:0] register_2_q, state_trans_1_s0_;
  wire [31:0] multiplexer_1_out, multiplexer_2_out, multiplexer_3_out, multiplexer_4_out, multiplexer_5_out,
       orig_matrix_1_o00, orig_matrix_1_o01, orig_matrix_1_o10, orig_matrix_1_o11, step_1_o00, step_1_o01,
       step_1_o10, step_1_o11, step_pff_1_o00, step_pff_1_o01, step_pff_1_o10, step_pff_1_o11,
       subtractor_1_out, zero_matrix_1_o00, zero_matrix_1_o01, zero_matrix_1_o10, zero_matrix_1_o11;

  Clock clock_1 (.out(clk));
  Register #(.width(1)) register_1 (.D(1'b1), .en(not_1_out), .Q(register_1_q), .clk(clk));  // open: clr
  not not_1 (not_1_out, register_1_q);
  not not_2 (not_2_out, register_1_q);
  Shift_Register #(.length(32)) shift_register_1 (
    .shift(register_1_q), .in(1'b0), .clk(clk), .out(shift_register_1_out), .load(not_2_out),
    .d0(subtractor_1_out[0]), .d1(subtractor_1_out[1]), .d2(subtractor_1_out[2]), .d3(subtractor_1_out[3]),
    .d4(subtractor_1_out[4]), .d5(subtractor_1_out[5]), .d6(subtractor_1_out[6]), .d7(subtractor_1_out[7]),
    .d8(subtractor_1_out[8]), .d9(subtractor_1_out[9]), .d10(subtractor_1_out[10]),
    .d11(subtractor_1_out[11]), .d12(subtractor_1_out[12]), .d13(subtractor_1_out[13]),
    .d14(subtractor_1_out[14]), .d15(subtractor_1_out[15]), .d16(subtractor_1_out[16]),
    .d17(subtractor_1_out[17]), .d18(subtractor_1_out[18]), .d19(subtractor_1_out[19]),
    .d20(subtractor_1_out[20]), .d21(subtractor_1_out[21]), .d22(subtractor_1_out[22]),
    .d23(subtractor_1_out[23]), .d24(subtractor_1_out[24]), .d25(subtractor_1_out[25]),
    .d26(subtractor_1_out[26]), .d27(subtractor_1_out[27]), .d28(subtractor_1_out[28]),
    .d29(subtractor_1_out[29]), .d30(subtractor_1_out[30]), .d31(subtractor_1_out[31]));  // open: clr, q0, q1, q2, q3, q4, q5, q6, q7, q8, q9, q10, q11, q12, q13, q14, q15, q16, q17, q18, q19, q20, q21, q22, q23, q24, q25, q26, q27, q28, q29, q30, q31
  Comparator #(.width(32), .mode("unsigned")) comparator_1 (.a(N), .b({32{1'b0}}), .eq(zero));  // open: gt, lt
  Comparator #(.width(32), .mode("unsigned")) comparator_2 (.a(N), .b(32'h1), .eq(one));  // open: gt, lt
  Subtractor #(.width(32)) subtractor_1 (.a(N), .b(32'h1), .out(subtractor_1_out));  // open: bin, bout
  Register #(.width(2)) register_2 (.D(state_trans_1_s0_), .Q(register_2_q), .clk(clk));  // open: en, clr
  state_trans state_trans_1 (
    .S1(register_2_q[1]), .S0(register_2_q[0]), .I(shift_register_1_out), .S1_(state_trans_1_s0_[1]),
    .S0_(state_trans_1_s0_[0]));
  // Probe on step_pff_1_o00
  // Probe on step_pff_1_o10
  Register #(.width(1)) \buf  (.D(shift_register_1_out), .Q(buf_q), .clk(clk));  // open: en, clr
  // Probe on register_2_q
  // Probe on step_pff_1_o01
  // Probe on step_pff_1_o11
  zero_matrix zero_matrix_1 (
    .o00(zero_matrix_1_o00), .o01(zero_matrix_1_o01), .o10(zero_matrix_1_o10), .o11(zero_matrix_1_o11));
  orig_matrix orig_matrix_1 (
    .o00(orig_matrix_1_o00), .o01(orig_matrix_1_o01), .o10(orig_matrix_1_o10), .o11(orig_matrix_1_o11));
  step step_1 (
    .i00(step_pff_1_o00), .i01(step_pff_1_o01), .i10(step_pff_1_o10), .i11(step_pff_1_o11), .curr_bit(buf_q),
    .o00(step_1_o00), .o01(step_1_o01), .o10(step_1_o10), .o11(step_1_o11));
  Counter #(.max('h22), .ongoal("stay")) counter_1 (
    .carry(counter_1_carry), .clk(clk));  // open: load, D, count, Q, clr
  Multiplexer #(.select(2), .width(32), .enable("false")) multiplexer_1 (
    .in0(zero_matrix_1_o00), .in1(orig_matrix_1_o00), .in2(step_1_o00), .out(multiplexer_1_out),
    .sel(register_2_q));  // open: in3
  Multiplexer #(.select(2), .width(32), .enable("false")) multiplexer_2 (
    .in0(zero_matrix_1_o01), .in1(orig_matrix_1_o01), .in2(step_1_o01), .out(multiplexer_2_out),
    .sel(register_2_q));  // open: in3
  Multiplexer #(.select(2), .width(32), .enable("false")) multiplexer_3 (
    .in0(zero_matrix_1_o10), .in1(orig_matrix_1_o10), .in2(step_1_o10), .out(multiplexer_3_out),
    .sel(register_2_q));  // open: in3
  Multiplexer #(.select(2), .width(32), .enable("false")) multiplexer_4 (
    .in0(zero_matrix_1_o11), .in1(orig_matrix_1_o11), .in2(step_1_o11), .out(multiplexer_4_out),
    .sel(register_2_q));  // open: in3
  or or_1 (or_1_out, counter_1_carry, zero, one);
  not not_3 (not_3_out, or_1_out);
  step_pff step_pff_1 (
    .i00(multiplexer_1_out), .i01(multiplexer_2_out), .i10(multiplexer_3_out), .i11(multiplexer_4_out),
    .clk(clk), .en(not_3_out), .o00(step_pff_1_o00), .o01(step_pff_1_o01), .o10(step_pff_1_o10),
    .o11(step_pff_1_o11));
  Multiplexer #(.width(32), .enable("false")) multiplexer_5 (
    .in0(step_pff_1_o00), .in1({32{1'b0}}), .out(multiplexer_5_out), .sel(not_3_out));
  Multiplexer #(.select(2), .width(32), .enable("false")) multiplexer_6 (
    .in0(multiplexer_5_out), .in1(32'h1), .in2({32{1'b0}}), .out(Nth), .sel({zero, one}));  // open: in3
endmodule

module matrix_squaring (
  input  [31:0] i00,
  input  [31:0] i01,
  input  [31:0] i10,
  input  [31:0] i11,
  output [31:0] o00,
  output [31:0] o01,
  output [31:0] o10,
  output [31:0] o11
);

  wire [31:0] multiplier_1_out, multiplier_2_out, multiplier_3_out, multiplier_4_out, multiplier_5_out,
       multiplier_6_out, multiplier_7_out, multiplier_8_out;

  Multiplier #(.width(32)) multiplier_1 (.a(i00), .b(i00), .out(multiplier_1_out));  // open: cin, cout
  Multiplier #(.width(32)) multiplier_2 (.a(i01), .b(i10), .out(multiplier_2_out));  // open: cin, cout
  Multiplier #(.width(32)) multiplier_3 (.a(i00), .b(i01), .out(multiplier_3_out));  // open: cin, cout
  Multiplier #(.width(32)) multiplier_4 (.a(i01), .b(i11), .out(multiplier_4_out));  // open: cin, cout
  Multiplier #(.width(32)) multiplier_5 (.a(i00), .b(i10), .out(multiplier_5_out));  // open: cin, cout
  Multiplier #(.width(32)) multiplier_6 (.a(i10), .b(i11), .out(multiplier_6_out));  // open: cin, cout
  Multiplier #(.width(32)) multiplier_7 (.a(i01), .b(i10), .out(multiplier_7_out));  // open: cin, cout
  Multiplier #(.width(32)) multiplier_8 (.a(i11), .b(i11), .out(multiplier_8_out));  // open: cin, cout
  Adder #(.width(32)) adder_1 (.a(multiplier_1_out), .b(multiplier_2_out), .out(o00));  // open: cin, cout
  Adder #(.width(32)) adder_2 (.a(multiplier_3_out), .b(multiplier_4_out), .out(o01));  // open: cin, cout
  Adder #(.width(32)) adder_3 (.a(multiplier_5_out), .b(multiplier_6_out), .out(o10));  // open: cin, cout
  Adder #(.width(32)) adder_4 (.a(multiplier_7_out), .b(multiplier_8_out), .out(o11));  // open: cin, cout
endmodule

module matrix_squaring_with_orig (
  input  [31:0] i00,
  input  [31:0] i01,
  input  [31:0] i10,
  input  [31:0] i11,
  output [31:0] o00,
  output [31:0] o01,
  output [31:0] o10,
  output [31:0] o11
);

  wire [31:0] matrix_squaring_1_o01, matrix_squaring_1_o11;

  matrix_squaring matrix_squaring_1 (
    .i00(i00), .i01(i01), .i10(i10), .i11(i11), .o00(o01), .o01(matrix_squaring_1_o01), .o10(o11),
    .o11(matrix_squaring_1_o11));
  Adder #(.width(32)) adder_1 (.a(o01), .b(matrix_squaring_1_o01), .out(o00));  // open: cin, cout
  Adder #(.width(32)) adder_2 (.a(o11), .b(matrix_squaring_1_o11), .out(o10));  // open: cin, cout
endmodule

module step (
  input  [31:0] i00,
  input  [31:0] i01,
  input  [31:0] i10,
  input  [31:0] i11,
  input  curr_bit,
  output [31:0] o00,
  output [31:0] o01,
  output [31:0] o10,
  output [31:0] o11
);

  wire [31:0] matrix_squaring_1_o00, matrix_squaring_1_o01, matrix_squaring_1_o10, matrix_squaring_1_o11,
       matrix_squaring_with_orig_1_o00, matrix_squaring_with_orig_1_o01, matrix_squaring_with_orig_1_o10,
       matrix_squaring_with_orig_1_o11;

  matrix_squaring matrix_squaring_1 (
    .i00(i00), .i01(i01), .i10(i10), .i11(i11), .o00(matrix_squaring_1_o00), .o01(matrix_squaring_1_o01),
    .o10(matrix_squaring_1_o10), .o11(matrix_squaring_1_o11));
  matrix_squaring_with_orig matrix_squaring_with_orig_1 (
    .i00(i00), .i01(i01), .i10(i10), .i11(i11), .o00(matrix_squaring_with_orig_1_o00),
    .o01(matrix_squaring_with_orig_1_o01), .o10(matrix_squaring_with_orig_1_o10),
    .o11(matrix_squaring_with_orig_1_o11));
  Multiplexer #(.width(32), .enable("false")) multiplexer_1 (
    .in0(matrix_squaring_1_o00), .in1(matrix_squaring_with_orig_1_o00), .out(o00), .sel(curr_bit));
  Multiplexer #(.width(32), .enable("false")) multiplexer_2 (
    .in0(matrix_squaring_1_o01), .in1(matrix_squaring_with_orig_1_o01), .out(o01), .sel(curr_bit));
  Multiplexer #(.width(32), .enable("false")) multiplexer_3 (
    .in0(matrix_squaring_1_o10), .in1(matrix_squaring_with_orig_1_o10), .out(o10), .sel(curr_bit));
  Multiplexer #(.width(32), .enable("false")) multiplexer_4 (
    .in0(matrix_squaring_1_o11), .in1(matrix_squaring_with_orig_1_o11), .out(o11), .sel(curr_bit));
endmodule

module step_pff (
  input  [31:0] i00,
  input  [31:0] i01,
  input  [31:0] i10,
  input  [31:0] i11,
  input  clk,
  input  en,
  output [31:0] o00,
  output [31:0] o01,
  output [31:0] o10,
  output [31:0] o11
);

  Register #(.width(32)) register_1 (.D(i00), .en(en), .Q(o00), .clk(clk));  // open: clr
  Register #(.width(32)) register_2 (.D(i01), .en(en), .Q(o01), .clk(clk));  // open: clr
  Register #(.width(32)) register_3 (.D(i10), .en(en), .Q(o10), .clk(clk));  // open: clr
  Register #(.width(32)) register_4 (.D(i11), .en(en), .Q(o11), .clk(clk));  // open: clr
endmodule

module orig_matrix (
  output [31:0] o00,
  output [31:0] o01,
  output [31:0] o10,
  output [31:0] o11
);


  assign o00 = 32'h1;
  assign o01 = 32'h1;
  assign o10 = 32'h1;
  assign o11 = {32{1'b0}};
endmodule

module zero_matrix (
  output [31:0] o00,
  output [31:0] o01,
  output [31:0] o10,
  output [31:0] o11
);


  assign o00 = {32{1'b0}};
  assign o01 = {32{1'b0}};
  assign o10 = {32{1'b0}};
  assign o11 = {32{1'b0}};
endmodule

module state_trans (
  input  S1,
  input  S0,
  input  I,
  output S1_,
  output S0_
);

  wire not_1_out, not_2_out;

  or or_1 (S1_, S0, S1);
  not not_1 (not_1_out, S1);
  not not_2 (not_2_out, S0);
  and and_1 (S0_, not_1_out, not_2_out, I);
endmodule
