// Logisim project mod5.circ as structural Verilog: 2 circuits, main circuit mod5
module mod5 (
  input  In,
  output S0,
  output S1,
  output S2,
  output S3,
  output S4
);

  wire clock_1_out;
  wire [1:0] register_1_q, state_trans_1_s0_;

  Register #(.width(2)) register_1 (
    .D(state_trans_1_s0_), .en(1'b1), .Q(register_1_q), .clk(clock_1_out));  // open: clr
  Clock clock_1 (.out(clock_1_out));
  state_trans state_trans_1 (
    .S1(register_1_q[1]), .S0(register_1_q[0]), .In(In), .S1_(state_trans_1_s0_[1]),
    .S0_(state_trans_1_s0_[0]));
  Decoder #(.select(2), .enable("false")) decoder_1 (
    .out0(S1), .out1(S2), .out2(S3), .out3(S4), .sel(state_trans_1_s0_));

  assign S0 = 1'b0;
endmodule

module state_trans (
  input  S1,
  input  S0,
  input  In,
  output S1_,
  output S0_
);

  wire and_1_out, and_2_out, and_3_out, and_4_out, and_5_out, and_6_out, not_1_out, not_2_out, not_3_out,
       not_4_out, not_5_out, not_6_out, not_7_out, not_8_out;

  not not_1 (not_1_out, S1);
  not not_2 (not_2_out, S0);
  not not_3 (not_3_out, S1);
  not not_4 (not_4_out, S0);
  not not_5 (not_5_out, S1);
  not not_6 (not_6_out, In);
  not not_7 (not_7_out, S0);
  not not_8 (not_8_out, In);
  and and_1 (and_1_out, not_1_out, S0);
  and and_2 (and_2_out, S1, not_2_out);
  and and_3 (and_3_out, not_3_out, not_4_out, In);
  and and_4 (and_4_out, not_5_out, S0, not_6_out);
  and and_5 (and_5_out, S1, not_7_out, not_8_out);
  and and_6 (and_6_out, S1, S0, In);
  or or_1 (S1_, and_1_out, and_2_out);
  or or_2 (S0_, and_3_out, and_4_out, and_5_out, and_6_out);
endmodule
